// Digital circuit 7segDispHex.dig as structural Verilog
module _7segDispHex (
  input  A,
  input  B,
  input  C,
  input  D,
  output out_a,
  output out_b,
  output out_c,
  output out_d,
  output out_e,
  output out_f,
  output out_g
);

  wire and_1_out, and_2_out, and_3_out, and_4_out, and_5_out, and_6_out, and_7_out, and_8_out, and_9_out,
       and_10_out, and_11_out, and_12_out, and_13_out, and_14_out, and_15_out, and_16_out, and_17_out,
       and_18_out, and_19_out, and_20_out, and_21_out, and_22_out, and_23_out, and_24_out, and_25_out,
       and_26_out, and_27_out, and_28_out, and_29_out, and_30_out, and_31_out, and_32_out, and_33_out,
       and_34_out, and_35_out, not_1_out, not_2_out, not_3_out, not_4_out, or_1_out;

  not not_1 (not_1_out, A);
  not not_2 (not_2_out, B);
  not not_3 (not_3_out, C);
  not not_4 (not_4_out, D);
  and and_1 (and_1_out, not_2_out, not_4_out);
  and and_2 (and_2_out, not_1_out, C);
  and and_3 (and_3_out, B, C);
  and and_4 (and_4_out, A, not_4_out);
  and and_5 (and_5_out, not_1_out, B, D);
  and and_6 (and_6_out, A, not_2_out, not_3_out);
  and and_7 (and_7_out, not_1_out, not_2_out);
  and and_8 (and_8_out, not_2_out, not_4_out);
  and and_9 (and_9_out, not_1_out, not_3_out, not_4_out);
  and and_10 (and_10_out, not_1_out, C, D);
  and and_11 (and_11_out, A, not_3_out, D);
  and and_12 (and_12_out, not_1_out, not_3_out);
  and and_13 (and_13_out, not_1_out, D);
  and and_14 (and_14_out, not_3_out, D);
  and and_15 (and_15_out, not_1_out, B);
  and and_16 (and_16_out, A, not_2_out);
  and and_17 (and_17_out, A, not_3_out);
  and and_18 (and_18_out, not_1_out, not_2_out, not_4_out);
  and and_19 (and_19_out, not_2_out, C, D);
  and and_20 (and_20_out, B, not_3_out, D);
  and and_21 (and_21_out, B, C, not_4_out);
  and and_22 (and_22_out, not_2_out, not_4_out);
  and and_23 (and_23_out, C, not_4_out);
  and and_24 (and_24_out, A, C);
  and and_25 (and_25_out, A, B);
  and and_26 (and_26_out, not_3_out, not_4_out);
  and and_27 (and_27_out, B, not_4_out);
  and and_28 (and_28_out, A, not_2_out);
  and and_29 (and_29_out, A, C);
  and and_30 (and_30_out, not_1_out, B, not_3_out);
  and and_31 (and_31_out, not_2_out, C);
  and and_32 (and_32_out, C, not_4_out);
  and and_33 (and_33_out, A, not_2_out);
  and and_34 (and_34_out, A, D);
  and and_35 (and_35_out, not_1_out, B, not_3_out);
  or or_1 (or_1_out, and_1_out, and_2_out, and_3_out, and_4_out, and_5_out);
  or or_2 (out_b, and_7_out, and_8_out, and_9_out, and_10_out, and_11_out);
  or or_3 (out_c, and_12_out, and_13_out, and_14_out, and_15_out, and_16_out);
  or or_4 (out_d, and_17_out, and_18_out, and_19_out, and_20_out, and_21_out);
  or or_5 (out_e, and_22_out, and_23_out, and_24_out, and_25_out);
  or or_6 (out_f, and_26_out, and_27_out, and_28_out, and_29_out, and_30_out);
  or or_7 (out_g, and_31_out, and_32_out, and_33_out, and_34_out, and_35_out);
  or or_8 (out_a, or_1_out, and_6_out);
endmodule
